// Logisim project circuitDesignNotForRelease-FirstIter.circ as structural Verilog: 1 circuit, main circuit main
module main (
  input  i_0,
  input  i_1,
  input  i_2,
  input  i_3,
  input  i_4,
  input  i_5,
  input  i_6,
  input  i_7,
  output LED
);

  wire and_1_out, and_2_out, and_3_out, and_4_out, not_1_out, not_2_out, not_3_out, not_4_out, or_1_out,
       xor_1_out, xor_2_out;

  not not_1 (not_1_out, i_5);
  and and_1 (and_1_out, i_1, i_6);
  xor xor_1 (xor_1_out, i_0, i_1);
  not not_2 (not_2_out, xor_1_out);
  or or_1 (or_1_out, i_2, i_3);
  and and_2 (and_2_out, i_4, i_6, i_7);
  and and_3 (and_3_out, not_2_out, or_1_out);
  not not_3 (not_3_out, i_2);
  not not_4 (not_4_out, i_4);
  and and_4 (and_4_out, i_0, not_3_out, not_4_out);
  xor xor_2 (xor_2_out, i_3, and_2_out);
  and and_5 (LED, and_3_out, and_4_out, and_1_out, xor_2_out, not_1_out);
endmodule
